# Fritzing sketch weather-station (saved by Fritzing 0.9.3b)
breadboards: 1

parts:
  Raspberry_Pi_Zero1 = Raspberry Pi Zero
  DHT1 = DHT11 Humitidy and Temperature Sensor
  IC1 = MCP3008 8-channel 10-bit ADC [part_number=MCP3008]
  Part1 = Adafruit BMP180
  Part2 = Ambient Light Sensor (TEMT6000 Breakout Board)
  Part3 = Soil Moisture Sensor

nets:
  N1: Raspberry_Pi_Zero1.GPIO2, Part1.SDA
  N2: Raspberry_Pi_Zero1.GPIO3, Part1.SCL
  N3: Raspberry_Pi_Zero1.GPIO4, DHT1.DATA
  N4: Raspberry_Pi_Zero1.GPIO17, Raspberry_Pi_Zero1.GPIO18, IC1.no_name_yet#13
  N5: Raspberry_Pi_Zero1.GPIO22, Raspberry_Pi_Zero1.GPIO23, IC1.no_name_yet#12
  N6: Raspberry_Pi_Zero1.3V3, Raspberry_Pi_Zero1.GPIO24, IC1.no_name_yet#11
  N7: Raspberry_Pi_Zero1.GPIO9, Raspberry_Pi_Zero1.GPIO25, IC1.no_name_yet#10
  GND: Raspberry_Pi_Zero1.GND, DHT1.GND, IC1.no_name_yet#14, Part1.GND, Part2.GND, Part3.GND
  VCC: Raspberry_Pi_Zero1.5V, DHT1.VDD, IC1.no_name_yet#9, IC1.no_name_yet#15, IC1.no_name_yet#16, Part1.+3V3, Part2.VCC, Part3.VCC
  N8: IC1.no_name_yet#1, Part2.S
  N9: IC1.no_name_yet#8, Part3.SIG

custom parts:
  DHT11 Humitidy and Temperature Sensor: DHT11 Humidity and Temperature Sensor
  Adafruit BMP180: This precision sensor from Bosch is the best low-cost sensing solution for measuring barometric pressure and temperature. Because pressure changes with altitude you can also use it as an altimeter! The sensor is soldered onto a PCB with a 3.3V regulator, I2C level shifter and pull-up resistors on the I2C pins. The BMP180 is the next-generation of sensors from Bosch, and replaces the BMP085.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
